# Fritzing sketch Capstone (saved by Fritzing 0.9.3b)

parts:
  Part1 = Arduino Uno (Rev3)
  Part2 = Arduino Uno (Rev3)
  Part6 = BigEasyDriver
  Part7 = LIDAR-Lite
  VCC1 = Battery
  R1 = Resistor [tolerance=±5% resistance=220 package=THT]
  LED1 = LED - 5mm [color="Red (633nm)" package="5 mm [THT]"]
  LED2 = LED - 5mm [color="Red (633nm)" package="5 mm [THT]"]
  C1 = Electrolytic Capacitor [capacitance=1µF package="100 mil [THT, electrolytic]"]
  J2 = Power Plug
  M1 = Stepper Motor - Bipolar

nets:
  GND: Part1.GND, Part2.GND, Part6.GND, Part7.GND, VCC1.-, LED1.cathode, LED2.anode, C1.-, J2.GND, J2.tip_GND
  N1: Part1.D0/RX, Part2.D1/TX
  N2: Part1.3V3, R1.Pin_0
  N3: Part2.A0, LED2.cathode
  N4: Part2.A4/SDA, Part7.SDA
  N5: Part2.A5/SCL, Part7.SCL
  N6: Part2.D2, Part6.STEP
  N7: Part2.D3_PWM, Part6.DIR
  N8: Part2.D4, Part6.MS1
  N9: Part2.D5_PWM, Part6.MS2
  N10: Part2.D6_PWM, Part6.MS3
  N11: Part2.D7, Part6.ENABLE
  5V: Part2.5V, Part7.5V, C1.+
  N12: Part6.COILB+, M1.A
  N13: Part6.COILB-, M1.C
  N14: Part6.COILA-, M1.B
  N15: Part6.COILA+, M1.D
  N16: Part6.2, VCC1.+, J2.PWR, J2.tip_PWR

custom parts:
  LIDAR-Lite: PulsedLight LIDAR-Lite Sensor
  Power Plug: Power Jack This is the standard 5.5mm barrel plug for power. This part has bendable leads (i.e. wires in the real world) to connect to wall warts or the breadboard in the standard wire end, and hidden connectors on the tip end that will connect when "plugged in" (overlapped with the jack so it appears "plugged in" in breadboard) to the modified coax jack part. Internal busses connect the two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
