# Fritzing sketch CapstoneWired (saved by Fritzing 0.9.3b)

parts:
  Part1 = Arduino Uno (Rev3)
  Part2 = Arduino Uno (Rev3)
  M2 = Stepper Motor - Bipolar
  Part6 = BigEasyDriver
  Part7 = LIDAR-Lite

nets:
  GND: Part1.GND, Part2.GND, Part6.GND, Part7.GND
  N1: Part1.D0/RX, Part2.D1/TX
  N2: Part2.A4/SDA, Part7.SDA
  N3: Part2.A5/SCL, Part7.SCL
  N4: Part2.D2, Part6.STEP
  N5: Part2.D3_PWM, Part6.DIR
  N6: Part2.D4, Part6.MS1
  N7: Part2.D5_PWM, Part6.MS2
  N8: Part2.D6_PWM, Part6.MS3
  N9: Part2.D7, Part6.ENABLE
  5V: Part2.5V, Part7.5V
  N10: M2.A, Part6.COILB+
  N11: M2.C, Part6.COILB-
  N12: M2.B, Part6.COILA-
  N13: M2.D, Part6.COILA+

custom parts:
  LIDAR-Lite: PulsedLight LIDAR-Lite Sensor
